# Fritzing sketch BaliRoads (saved by Fritzing 0.9.3b)

parts:
  U1 = NodeMCU V1.0
  Composant1 = 16-Channel 12-bit PWM Servo Driver - I2C [part_number=815]
  Q1 = MOSFET-NCHANNEL [package=to220v]
  Q2 = MOSFET-NCHANNEL [package=to220v]
  Q3 = MOSFET-NCHANNEL [package=to220v]
  HLK-PM1 = HLK-PM12 [part_number=HLK-PM12]
  LED1 = LEDs [package=led10mm]
  LED2 = LEDs [package=led10mm]
  LED3 = LEDs [package=led10mm]
  HLK-PM2 = HLK-PM01
  Composant2 = 16-Channel 12-bit PWM Servo Driver - I2C [part_number=815]

nets:
  N1: U1.D1, Composant1.SCL, Composant2.SCL
  N2: U1.D2, Composant1.SDA, Composant2.SDA
  VCC: U1.3V3, Composant1.VCC, Composant2.VCC
  GND: U1.GND, Composant1.GND, Q1.G, Q1.S, Q2.G, Q2.S, Q3.G, Q3.S, HLK-PM1.-Vo, HLK-PM2.-Vo, Composant2.GND
  N3: U1.Vin, HLK-PM2.+Vo
  N4: Q1.D, LED1.C
  N5: Q2.D, LED2.C
  N6: Q3.D, LED3.C
  N7: HLK-PM1.+Vo, LED1.A, LED2.A, LED3.A

custom parts:
  NodeMCU V1.0: ESP8266 based NodeMCU
  16-Channel 12-bit PWM Servo Driver - I2C: You want to make a cool robot, maybe a hexapod walker, or maybe just a piece of art with a lot of moving parts. Or maybe you want to drive a lot of LEDs with precise PWM output. Using only two pins, control 16 free-running PWM outputs! You can even chain up 62 breakouts to control up to 992 PWM outputs.
